# Fritzing sketch Diagrmama_conexiones (saved by Fritzing 1.0.4)

parts:
  U1 = SWITCH-SPST-2 [package=switch-spst-vertical]  # not connected
  M1 = TP4056 Module [part_number=HW-107]
  U3 = LIPO-1000mAh [package=lipo-1000]
  M2 = gear-motor

nets:
  N1: M1.OUT-#1, M2.pin_2
  N2: M1.BAT-, U3.-
  N3: M1.OUT-#4, M2.pin_1

custom parts:
  TP4056 Module: TP4056 Lithium Battery Charge Management Module Links: TP4056 website
